// Digital circuit 4 BIT ADDER-SUBTRACTOR.dig as structural Verilog
module _4_BIT_ADDER_SUBTRACTOR (
  input  [3:0] A,
  input  [3:0] B,
  input  S,
  output [3:0] Sum
);

  wire _1_bit_full_adder_1_p3, _1_bit_full_adder_2_p3, _1_bit_full_adder_3_p3, xor_1_out, xor_2_out,
       xor_3_out, xor_4_out;

  xor xor_1 (xor_1_out, B[3], S);
  xor xor_2 (xor_2_out, B[2], S);
  // _1_bit_full_adder _1_bit_full_adder_1: pin names not known; wires that end beside it: A[3], xor_1_out, _1_bit_full_adder_1_p3, Sum[3]
  // _1_bit_full_adder _1_bit_full_adder_2: pin names not known; wires that end beside it: A[2], xor_2_out, _1_bit_full_adder_2_p3, Sum[2], _1_bit_full_adder_1_p3
  xor xor_3 (xor_3_out, B[1], S);
  xor xor_4 (xor_4_out, B[0], S);
  // _1_bit_full_adder _1_bit_full_adder_3: pin names not known; wires that end beside it: A[1], xor_3_out, _1_bit_full_adder_3_p3, Sum[1], _1_bit_full_adder_2_p3
  // _1_bit_full_adder _1_bit_full_adder_4: pin names not known; wires that end beside it: A[0], xor_4_out, S, Sum[0], _1_bit_full_adder_3_p3
endmodule
